# Fritzing sketch Robot pompier (saved by Fritzing 0.9.3b)
circuit board: 8.46667cm x 5.64444cm

parts:
  Part1 = Arduino Nano (Rev3.0)
  L298N1 = L298N DC motor driver
  M1 = DC Motor
  M2 = DC Motor
  Mod1 = KY-026 Flame Sensor Module [package="Breakout board"]
  Part2 = MQ-4
  VCC3 = Battery block 9V
  DHT1 = DHT11 Humitidy and Temperature Sensor (3 pins)
  J1 = Basic Servo  # not connected
  S1 = SWITCH-MOMENTARY-2 [package=tactile-switch-1101ne]
  Mod2 = KY-022 Infrared Receiver Module [package="Breakout board"]

nets:
  N1: Part1.D1/TX, Part1.D2, L298N1.IN1
  N2: Part1.D3, L298N1.IN2
  N3: Part1.D4, L298N1.IN3
  N4: Part1.D5, L298N1.IN4
  N5: Part1.D6, Mod1.D0
  N6: Part1.D7, Part2.DO
  N7: Part1.D8, DHT1.Signal
  N8: Part1.D9, L298N1.ENA
  N9: Part1.D10, L298N1.ENB
  N10: Part1.D11/MOSI, Mod2.S
  N11: Part1.D12/MISO, S1.1
  GND: Part1.GND, L298N1.GND, Mod1.G, VCC3.-
  5V: Part1.5V, L298N1.5V, Mod1.+, DHT1.Plus
  N12: Part1.A5, Part2.AO
  N13: L298N1.OUT1, M1.pin_2
  N14: L298N1.OUT2, M1.pin_1
  N15: L298N1.OUT3, M2.pin_2
  N16: L298N1.OUT4, M2.pin_1
  VCC: Part2.VCC, Mod2.Vin
  N17: Part2.GND, Mod2.-
  N18: DHT1.Gnd, S1.2

custom parts:
  L298N DC motor driver: 2x DC motor driver with 78M05 positive voltage regulator (7..35 V) L298N: max 46 V, 2 A Set 5 V Enable jumper to enable 5 V regultor (needed for the L298N) and +5 V output at screw terminal or supply external +5 V at screw terminal Set ENA and/or ENB to +5 V to enable motor permanently or supply ENA and/or ENB with PWM signal IN1 and IN2 set rotation directory for motor A (OUT1/OUT2) IN2 and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
  KY-026 Flame Sensor Module: KY-026 Flame Sensor Module reacts in the presence of fire.
  DHT11 Humitidy and Temperature Sensor (3 pins): DHT11 Humidity and Temperature Sensor (3 pins).
  KY-022 Infrared Receiver Module: KY-022 IR receiver module, reacts to 38kHz infrared light.

// code stored in the sketch: Drive.ino
int motor1pin1 =2;
int motor1pin2 =3;
int motor2pin1 =4;
int motor2pin2 =5;
int control1=9;
int control2=10;
int flacara=6;
int dht11=8;
void setup(){
	pinMode(motor1pin1, OUTPUT);
	pinMode(motor1pin2, OUTPUT);
	pinMode(motor2pin1, OUTPUT);
	pinMode(motor2pin2, OUTPUT);
	pinMode(control1, OUTPUT);
	pinMode(control2, OUTPUT);
  pinMode(flacara, INPUT);
  pinMode(dht11, INPUT);
}
void fata(int x){
	analogWrite(control1, x);
	analogWrite(control2, x);
	digitalWrite(motor1pin1, HIGH);
	digitalWrite(motor1pin2, LOW);
	digitalWrite(motor2pin1, HIGH);
	digitalWrite(motor2pin2, LOW);
	
}
void spate(int x){
	analogWrite(control1, x);
	analogWrite(control2, x);
	digitalWrite(motor1pin1, LOW);
	digitalWrite(motor1pin2, HIGH);
	digitalWrite(motor2pin1, LOW);
	digitalWrite(motor2pin2, HIGH);
	
}
void stanga(int x){
	analogWrite(control1, x);
	analogWrite(control2, x);
	digitalWrite(motor1pin1, HIGH);
	digitalWrite(motor1pin2, LOW);
	digitalWrite(motor2pin1, LOW);
	digitalWrite(motor2pin2, HIGH);
	
}
void dreapta(int x){
	analogWrite(control1, x);
	analogWrite(control2, x);
	digitalWrite(motor1pin1, LOW);
	digitalWrite(motor1pin2, HIGH);
	digitalWrite(motor2pin1, HIGH);
	digitalWrite(motor2pin2, LOW);
	
}
void stop(int x){
  analogWrite(control1, 0);
  analogWrite(control2, 0);
  digitalWrite(motor1pin1, LOW);
  digitalWrite(motor1pin2, LOW);
  digitalWrite(motor2pin1, LOW);
  digitalWrite(motor2pin2, LOW);
  
}

void loop()
{
  int x=100;
  //if(digitalRead(flacara)==LOW)
  fata(x);
  //else
  //stop(x);
}
